// Logisim project cpu.circ as structural Verilog
module B_machine (
);

  wire BSEL, RA2SEL, WERF, WR, Z;
  wire [1:0] PCSEL, WDSEL;
  wire [3:0] ALUFN;
  wire [4:0] multiplexer_3_out;
  wire [31:0] alu_1_out_4, bit_extender_1_out, data_memory_1_rd, instruction_memory_1_out_2, JT,
       literal_multiplication_1_new_pc_value, multiplexer_1_out, multiplexer_2_out, multiplexer_4_out,
       n4_1_out_2, pc_1_out_2, register_file_1_out_6, register_file_1_out_7;

  Multiplexer #(.select(2), .width(32)) multiplexer_1 (
    .in0(n4_1_out_2), .in1(literal_multiplication_1_new_pc_value), .in2(JT), .out(multiplexer_1_out),
    .sel(PCSEL));  // open: in3, en
  PC pc_1 (.in_1(multiplexer_1_out), .out_2(pc_1_out_2));
  _4 u_4_1 (.in_1(pc_1_out_2), .out_2(n4_1_out_2));
  Literal_Multiplication literal_multiplication_1 (
    .PC_4(n4_1_out_2), .Literal(instruction_memory_1_out_2),
    .New_PC_value(literal_multiplication_1_new_pc_value));
  Instruction_Memory instruction_memory_1 (.in_1(pc_1_out_2), .out_2(instruction_memory_1_out_2));
  Control_Logic control_logic_1 (
    .opcode(instruction_memory_1_out_2[31:26]), .control({PCSEL, RA2SEL, WR, WDSEL, BSEL, WERF, ALUFN}), .z(Z));
  assign bit_extender_1_out = {{16{instruction_memory_1_out_2[15]}}, instruction_memory_1_out_2[15:0]};  // Bit_Extender bit_extender_1
  NOR32bits nor32bits_1 (.in_1(register_file_1_out_6), .out_2(Z));
  assign JT = register_file_1_out_6 & 32'hfffffffc;  // AND_Gate and_1, 32 bits wide
  Register_File register_file_1 (
    .WE(WERF), .WA(instruction_memory_1_out_2[25:21]), .WD(multiplexer_2_out),
    .RA1(instruction_memory_1_out_2[20:16]), .RA2(multiplexer_3_out), .out_6(register_file_1_out_6),
    .out_7(register_file_1_out_7));
  ALU alu_1 (.out_4(alu_1_out_4), .RA1(ALUFN), .A(register_file_1_out_6), .B(multiplexer_4_out));
  Multiplexer #(.select(2), .width(32)) multiplexer_2 (
    .in0(n4_1_out_2), .in1(alu_1_out_4), .in2(data_memory_1_rd), .out(multiplexer_2_out), .sel(WDSEL));  // open: in3, en
  Multiplexer #(.width(5)) multiplexer_3 (
    .in0(instruction_memory_1_out_2[15:11]), .in1(instruction_memory_1_out_2[25:21]),
    .out(multiplexer_3_out), .sel(RA2SEL));  // open: en
  Multiplexer #(.width(32)) multiplexer_4 (
    .in0(bit_extender_1_out), .in1(register_file_1_out_7), .out(multiplexer_4_out), .sel(BSEL));  // open: en
  Data_memory data_memory_1 (.Addr(alu_1_out_4), .WD(register_file_1_out_7), .RD(data_memory_1_rd), .WR(WR));

  // Notes on the sheet:
  //   For operations
  //   To store operations result
  //   For operations with constant
endmodule

module ALU (
  input  [31:0] A,
  input  [31:0] B,
  input  [3:0] RA1,
  output [31:0] out_4
);

  wire comparator_1_eq, comparator_1_lt, or_2_out;
  wire [31:0] adder_1_out, and_1_out, bit_extender_1_out, bit_extender_2_out, bit_extender_3_out,
       divider_1_out, multiplier_1_out, or_1_out, shifter_1_out, shifter_2_out, shifter_3_out,
       subtractor_1_out, xor_1_out;

  Multiplier #(.width(32)) multiplier_1 (.a(A), .b(B), .out(multiplier_1_out));  // open: cin, cout
  Subtractor #(.width(32)) subtractor_1 (.a(A), .b(B), .out(subtractor_1_out));  // open: bin, bout
  Adder #(.width(32)) adder_1 (.a(A), .b(B), .out(adder_1_out));  // open: cin, cout
  Divider #(.width(32)) divider_1 (.a(A), .b(B), .out(divider_1_out));  // open: upper, rem
  assign and_1_out = A & B;  // AND_Gate and_1, 32 bits wide
  Multiplexer #(.select(4), .width(32)) multiplexer_1 (
    .in1(adder_1_out), .in2(subtractor_1_out), .in3(multiplier_1_out), .in4(divider_1_out), .in5(and_1_out),
    .in6(or_1_out), .in7(xor_1_out), .in8(bit_extender_1_out), .in9(bit_extender_2_out),
    .in10(bit_extender_3_out), .in11(shifter_3_out), .in12(shifter_2_out), .in13(shifter_1_out), .out(out_4),
    .sel(RA1));  // open: in0, in14, in15, en
  assign or_1_out = A | B;  // OR_Gate or_1, 32 bits wide
  assign xor_1_out = A ^ B;  // XOR_Gate xor_1, 32 bits wide
  assign bit_extender_1_out = {{31{1'b0}}, comparator_1_eq};  // Bit_Extender bit_extender_1
  Comparator #(.width(32)) comparator_1 (.a(A), .b(B), .eq(comparator_1_eq), .lt(comparator_1_lt));  // open: gt
  assign bit_extender_2_out = {{31{1'b0}}, comparator_1_lt};  // Bit_Extender bit_extender_2
  or or_2 (or_2_out, comparator_1_lt, comparator_1_eq);
  assign bit_extender_3_out = {{31{1'b0}}, or_2_out};  // Bit_Extender bit_extender_3
  Shifter #(.width(32), .shift("ar")) shifter_1 (.in(A), .\dist (B[4:0]), .out(shifter_1_out));
  Shifter #(.width(32), .shift("lr")) shifter_2 (.in(A), .\dist (B[4:0]), .out(shifter_2_out));
  Shifter #(.width(32)) shifter_3 (.in(A), .\dist (B[4:0]), .out(shifter_3_out));
endmodule

module Register_File (
  input  WE,
  input  [4:0] WA,
  input  [31:0] WD,
  input  [4:0] RA1,
  input  [4:0] RA2,
  output [31:0] out_6,
  output [31:0] out_7
);

  wire clock_1_out, demultiplexer_1_out0, demultiplexer_1_out1, demultiplexer_1_out2, demultiplexer_1_out3,
       demultiplexer_1_out4, demultiplexer_1_out29, demultiplexer_1_out30;
  wire [31:0] register_1_q, register_2_q, register_3_q, register_4_q, register_5_q, register_6_q,
       register_7_q;

  Clock clock_1 (.out(clock_1_out));
  Register #(.width(32)) register_1 (
    .D(WD), .en(demultiplexer_1_out1), .Q(register_1_q), .clk(clock_1_out));  // open: clr
  Register #(.width(32)) register_2 (
    .D(WD), .en(demultiplexer_1_out0), .Q(register_2_q), .clk(clock_1_out));  // open: clr
  Multiplexer #(.select(5), .width(32)) multiplexer_1 (
    .in0(register_2_q), .in1(register_1_q), .in2(register_3_q), .in3(register_4_q), .in4(register_5_q),
    .in29(register_6_q), .in30(register_7_q), .in31({32{1'b0}}), .out(out_6), .sel(RA1));  // open: in5, in6, in7, in8, in9, in10, in11, in12, in13, in14, in15, in16, in17, in18, in19, in20, in21, in22, in23, in24, in25, in26, in27, in28, en
  Demultiplexer #(.select(5)) demultiplexer_1 (
    .out0(demultiplexer_1_out0), .out1(demultiplexer_1_out1), .out2(demultiplexer_1_out2),
    .out3(demultiplexer_1_out3), .out4(demultiplexer_1_out4), .out29(demultiplexer_1_out29),
    .out30(demultiplexer_1_out30), .in(WE), .sel(WA));  // open: out5, out6, out7, out8, out9, out10, out11, out12, out13, out14, out15, out16, out17, out18, out19, out20, out21, out22, out23, out24, out25, out26, out27, out28, out31, en
  Register #(.width(32)) register_3 (
    .D(WD), .en(demultiplexer_1_out2), .Q(register_3_q), .clk(clock_1_out));  // open: clr
  Register #(.width(32)) register_4 (
    .D(WD), .en(demultiplexer_1_out3), .Q(register_4_q), .clk(clock_1_out));  // open: clr
  Register #(.width(32)) register_5 (
    .D(WD), .en(demultiplexer_1_out4), .Q(register_5_q), .clk(clock_1_out));  // open: clr
  Register #(.width(32)) register_6 (
    .D(WD), .en(demultiplexer_1_out29), .Q(register_6_q), .clk(clock_1_out));  // open: clr
  Register #(.width(32)) register_7 (
    .D(WD), .en(demultiplexer_1_out30), .Q(register_7_q), .clk(clock_1_out));  // open: clr
  Multiplexer #(.select(5), .width(32)) multiplexer_2 (
    .in0(register_2_q), .in1(register_1_q), .in2(register_3_q), .in3(register_4_q), .in4(register_5_q),
    .in29(register_6_q), .in30(register_7_q), .in31({32{1'b0}}), .out(out_7), .sel(RA2));  // open: in5, in6, in7, in8, in9, in10, in11, in12, in13, in14, in15, in16, in17, in18, in19, in20, in21, in22, in23, in24, in25, in26, in27, in28, en

  // Notes on the sheet:
  //   RD1
  //   RD2
endmodule

module Instruction_Memory (
  input  [31:0] in_1,
  output [31:0] out_2
);

  ROM #(.dataWidth(32)) rom_1 (.addr(in_1[9:2]), .data(out_2));  // open: sel

  // Notes on the sheet:
  //   contents of rom_1 (hex, n*v repeats v):
  //   c01f0003 c03f0001 77e00004 88210000 c4000001 77e00001 77fffffc 643f0000
endmodule

module PC (
  input  [31:0] in_1,
  output [31:0] out_2
);

  wire clock_1_out;

  Register #(.width(32)) register_1 (.D(in_1), .Q(out_2), .clk(clock_1_out));  // open: en, clr
  Clock clock_1 (.out(clock_1_out));

  // Notes on the sheet:
  //   Always multiple of 4 -> the two least significant bits are 0
endmodule

module _4 (
  input  [31:0] in_1,
  output [31:0] out_2
);

  Adder #(.width(32)) adder_1 (.a(in_1), .b(32'h4), .out(out_2));  // open: cin, cout
endmodule

module Control_Logic (
  input  [5:0] opcode,
  input  z,
  output [11:0] control
);

  wire not_1_out;
  wire [1:0] bit_extender_1_out, bit_extender_2_out;
  wire [11:0] rom_1_data;

  not not_1 (not_1_out, z);
  assign bit_extender_1_out = {{1{1'b0}}, z};  // Bit_Extender bit_extender_1
  assign bit_extender_2_out = {{1{1'b0}}, not_1_out};  // Bit_Extender bit_extender_2
  ROM #(.addrWidth(6), .dataWidth(12)) rom_1 (.addr(opcode), .data(rom_1_data));  // open: sel
  Multiplexer #(.select(2), .width(12)) multiplexer_1 (
    .in0(rom_1_data), .in1({2'b10, rom_1_data[9:0]}), .in2({bit_extender_1_out, rom_1_data[9:0]}),
    .in3({bit_extender_2_out, rom_1_data[9:0]}), .out(control), .sel(rom_1_data[11:10]));  // open: en

  // Notes on the sheet:
  //   contents of rom_1 (hex, n*v repeats v):
  //   24*0 91 301 0 410 0 810 c10 0 71 72 73 74 78 79 7a 0 75 76 77 0 7b 7c 7d 0 51 52 53 54 58 59 5a 0 55
  //   56 57 0 5b 5c 5d
endmodule

module NOR32bits (
  input  [31:0] in_1,
  output out_2
);

  Comparator #(.width(32), .mode("unsigned")) comparator_1 (.a({32{1'b0}}), .b(in_1), .eq(out_2));  // open: gt, lt
endmodule

module Literal_Multiplication (
  input  [31:0] PC_4,
  input  [31:0] Literal,
  output [31:0] New_PC_value
);

  wire [31:0] bit_extender_1_out, multiplier_1_out;

  Multiplier #(.width(32)) multiplier_1 (.a(32'h4), .b(bit_extender_1_out), .out(multiplier_1_out));  // open: cin, cout
  assign bit_extender_1_out = {{16{1'b0}}, Literal[15:0]};  // Bit_Extender bit_extender_1
  Adder #(.width(32)) adder_1 (.a(PC_4), .b(multiplier_1_out), .out(New_PC_value));  // open: cin, cout
endmodule

module Data_memory (
  input  [31:0] Addr,
  input  [31:0] WD,
  input  WR,
  output [31:0] RD
);

  wire clock_1_out, not_1_out;

  Clock clock_1 (.out(clock_1_out));
  not not_1 (not_1_out, WR);
  RAM #(.dataWidth(32), .bus("separate")) ram_1 (
    .addr(Addr[9:2]), .din(WD), .data(RD), .str(WR), .clk(clock_1_out), .ld(not_1_out));  // open: sel, clr
endmodule
